# Fritzing sketch Schematic (saved by Fritzing 0.7.10b)

parts:
  Arduino1 = Arduino
  Part1 = Bluetooth Mate Silver
  IR1 = TSOP312.., 314.. [package=THT]
  R1 = 680 Ω Resistor [package=THT]
  R2 = 680 Ω Resistor [package=THT]
  R3 = 680 Ω Resistor [package=THT]
  LED2 = RGB LED (com. cathode, rbg) [package="5 mm [THT]"]
  J1 = Basic Servo

nets:
  GND: Arduino1.GND, Part1.GND, J1.gnd
  N1: Arduino1.D11, J1.pulse
  N2: Arduino1.D9, IR1.Data
  N3: Arduino1.D8, R3.Pin_1
  N4: Arduino1.D7, R2.Pin_1
  N5: Arduino1.D6, R1.Pin_1
  N6: Arduino1.D1TX, Part1.RX_5V
  N7: Arduino1.D0RX, Part1.TX_5V
  N8: Arduino1.+5V, LED2.common_cathode
  N9: IR1.Vs, J1.vcc
